// Logisim project proj3.circ as structural Verilog: 1 circuit, main circuit main
module main (
  input  [7:0] in_1,
  input  [7:0] in_2,
  input  in_3,
  input  [7:0] in_4,
  input  [7:0] in_5,
  output [7:0] out_6,
  output [7:0] out_7,
  output [1:0] out_8,
  output [7:0] out_9
);

  wire button_1_out, clock_1_out, comparator_1_lt;
  wire [7:0] adder_1_out, adder_2_out, adder_3_out, multiplexer_1_out, multiplexer_2_out, not_1_out,
       register_1_q, register_2_q, subtractor_1_out;

  Register register_1 (.D(adder_1_out), .en(in_3), .clk(clock_1_out), .Q(register_1_q), .clr(button_1_out));
  Adder adder_1 (.a(in_1), .b(register_1_q), .out(adder_1_out), .cin(in_3));  // open: cout
  Clock clock_1 (.out(clock_1_out));
  Button button_1 (.out(button_1_out));
  ROM rom_1 (.addr(register_1_q), .data(out_6));
  assign out_7 = {{2{out_6[5]}}, out_6[5:0]};  // Bit_Extender bit_extender_1
  Register register_2 (.D(out_9), .en(clock_1_out), .clk(clock_1_out), .Q(register_2_q));  // open: clr
  Adder adder_2 (.a(register_2_q), .b(out_7), .out(adder_2_out));  // open: cin, cout
  Subtractor subtractor_1 (.a(register_2_q), .b(out_7), .out(subtractor_1_out));  // open: bin, bout
  assign not_1_out = ~register_2_q;  // NOT_Gate not_1, 8 bits wide
  Comparator comparator_1 (.a(register_2_q), .b(in_4), .lt(comparator_1_lt));  // open: gt, eq
  Adder adder_3 (.a(not_1_out), .b(in_2), .out(adder_3_out));  // open: cin, cout
  Multiplexer #(.width(8)) multiplexer_1 (
    .in0(register_2_q), .in1(adder_3_out), .out(multiplexer_1_out), .sel(comparator_1_lt));
  Multiplexer #(.width(8)) multiplexer_2 (
    .in0(register_2_q), .in1(in_5), .out(multiplexer_2_out), .sel(comparator_1_lt));
  Multiplexer #(.select(2), .width(8)) multiplexer_3 (
    .in0(adder_2_out), .in1(subtractor_1_out), .in2(multiplexer_1_out), .in3(multiplexer_2_out), .out(out_9),
    .sel(out_6[7:6]));

  assign out_8 = out_6[7:6];

  // Notes on the sheet:
  //   contents of rom_1 (hex, n*v repeats v):
  //   61 ee 36 7f
endmodule
